// Logisim project 1-1.circ as structural Verilog: 1 circuit, main circuit main
// F
module main (
  input  in_1,
  input  in_2,
  input  Z,
  output out_4
);

  wire X_Y_out, X_Z_out, Y_Z_out;

  and X_Z (X_Z_out, in_1, Z);
  and X_Y (X_Y_out, in_1, in_2);
  and Y_Z (Y_Z_out, in_2, Z);
  or or_1 (out_4, X_Z_out, X_Y_out, Y_Z_out);

  // Notes on the sheet:
  //   X
  //   Y
  //   多数表决器 F= Y ∙ Z+ X ∙ Z+ X ∙ Y
endmodule
