// Logisim project 1-5-1.circ as structural Verilog: 1 circuit, main circuit main
module main (
  input  N0,
  input  N1,
  input  N2,
  input  N3,
  output ODD,
  output EVEN
);

  wire xor_1_out, xor_2_out;

  xor xor_1 (xor_1_out, N0, N1);
  xor xor_2 (xor_2_out, N2, N3);
  xor xor_3 (ODD, xor_1_out, xor_2_out);
  not not_1 (EVEN, ODD);

  // Notes on the sheet:
  //   4位奇偶校验电路
endmodule
