// Logisim project 4-1MUX.circ as structural Verilog: 3 circuits, main circuit 8-1MUX
module _4_1MUX (
  input  D0,
  input  D1,
  input  D2,
  input  D3,
  input  S0,
  input  S1,
  output Y
);

  wire n2_1mux_1_y, n2_1mux_2_y;

  _2_1MUX u_2_1mux_1 (.D0(D2), .D1(D3), .S(S0), .Y(n2_1mux_1_y));
  _2_1MUX u_2_1mux_2 (.D0(D0), .D1(D1), .S(S0), .Y(n2_1mux_2_y));
  _2_1MUX u_2_1mux_3 (.D0(n2_1mux_2_y), .D1(n2_1mux_1_y), .S(S1), .Y(Y));

  // Notes on the sheet:
  //   2-1MUX
  //   2-1MUX
  //   四选一多路选择器
  //   2-1MUX
endmodule

module _2_1MUX (
  input  D0,
  input  D1,
  input  S,
  output Y
);

  wire transistor_1_out;

  Transistor transistor_1 (.in(1'b1), .out(transistor_1_out), .gate(S));
  Transistor #(.\type ("n")) transistor_2 (.in(1'b0), .out(transistor_1_out), .gate(S));
  // Transmission_Gate transmission_1: pin names not known; wires that end beside it: D0, S, transistor_1_out, Y
  // Transmission_Gate transmission_2: pin names not known; wires that end beside it: D1, transistor_1_out, S, Y

  // Notes on the sheet:
  //   二选一多路选择器
endmodule

module _8_1MUX (
  input  D0,
  input  D1,
  input  D2,
  input  D3,
  input  D4,
  input  D5,
  input  D6,
  input  D7,
  input  in_9,
  input  S1,
  input  S2,
  output out_12
);

  wire n4_1mux_1_y, n4_1mux_2_y;

  _4_1MUX u_4_1mux_1 (.D0(D0), .D1(D1), .D2(D2), .D3(D3), .S0(in_9), .S1(S1), .Y(n4_1mux_1_y));
  _4_1MUX u_4_1mux_2 (.D0(D4), .D1(D5), .D2(D6), .D3(D7), .S0(in_9), .S1(S1), .Y(n4_1mux_2_y));
  _2_1MUX u_2_1mux_1 (.D0(n4_1mux_1_y), .D1(n4_1mux_2_y), .S(S2), .Y(out_12));

  // Notes on the sheet:
  //   S0
endmodule
