// Logisim project lab3.1.circ as structural Verilog: 2 circuits, main circuit 4位同步二进制计数器
module \_4位同步二进制计数器  (
  input  CLK,
  input  LD,
  input  CLR,
  input  D0,
  input  D1,
  input  D2,
  input  D3,
  input  ENP,
  input  ENT,
  output Q,
  output Q1,
  output Q2,
  output Q3,
  output RCO
);

  wire and_1_out, and_2_out, and_3_out, and_4_out, and_5_out, and_6_out, and_7_out, and_8_out, and_10_out,
       and_11_out, and_12_out, and_13_out, and_14_out, and_15_out, and_16_out, and_17_out, buffer_1_out,
       d_ff_1_qn, d_ff_2_qn, d_ff_3_qn, d_ff_4_qn, not_1_out, not_2_out, not_3_out, or_1_out, or_2_out,
       or_3_out, or_4_out, xor_1_out, xor_2_out, xor_3_out, xor_4_out;

  buf buffer_1 (buffer_1_out, CLR);
  not not_1 (not_1_out, d_ff_1_qn);
  and and_1 (and_1_out, ~d_ff_2_qn, ~d_ff_1_qn);  // AND_Gate
  and and_2 (and_2_out, ~d_ff_3_qn, ~d_ff_2_qn, ~d_ff_1_qn);  // AND_Gate
  and and_3 (and_3_out, ENP, ENT);
  not not_2 (not_2_out, CLK);
  and and_4 (and_4_out, not_1_out, and_3_out);
  and and_5 (and_5_out, and_1_out, and_3_out);
  and and_6 (and_6_out, and_2_out, and_3_out);
  not not_3 (not_3_out, ENT);
  and and_7 (and_7_out, LD, ~buffer_1_out);  // AND_Gate
  and and_8 (and_8_out, ~and_7_out, ~buffer_1_out);  // AND_Gate
  xor xor_1 (xor_1_out, and_3_out, ~d_ff_1_qn);  // XOR_Gate
  xor xor_2 (xor_2_out, and_4_out, ~d_ff_2_qn);  // XOR_Gate
  xor xor_3 (xor_3_out, and_5_out, ~d_ff_3_qn);  // XOR_Gate
  xor xor_4 (xor_4_out, and_6_out, ~d_ff_4_qn);  // XOR_Gate
  and and_9 (RCO, ~d_ff_4_qn, ~d_ff_3_qn, ~d_ff_2_qn, ~d_ff_1_qn, ~not_3_out);  // AND_Gate
  and and_10 (and_10_out, and_7_out, D0);
  and and_11 (and_11_out, and_8_out, xor_1_out);
  and and_12 (and_12_out, and_7_out, D1);
  and and_13 (and_13_out, and_8_out, xor_2_out);
  and and_14 (and_14_out, and_7_out, D2);
  and and_15 (and_15_out, and_8_out, xor_3_out);
  and and_16 (and_16_out, and_7_out, D3);
  and and_17 (and_17_out, and_8_out, xor_4_out);
  or or_1 (or_1_out, and_10_out, and_11_out);
  or or_2 (or_2_out, and_12_out, and_13_out);
  or or_3 (or_3_out, and_14_out, and_15_out);
  or or_4 (or_4_out, and_16_out, and_17_out);
  D_Flip_Flop d_ff_1 (.clk(not_2_out), .D(or_1_out), .Q(Q), .Qn(d_ff_1_qn));  // open: preset, reset
  D_Flip_Flop d_ff_2 (.clk(not_2_out), .D(or_2_out), .Q(Q1), .Qn(d_ff_2_qn));  // open: preset, reset
  D_Flip_Flop d_ff_3 (.clk(not_2_out), .D(or_3_out), .Q(Q2), .Qn(d_ff_3_qn));  // open: preset, reset
  D_Flip_Flop d_ff_4 (.clk(not_2_out), .D(or_4_out), .Q(Q3), .Qn(d_ff_4_qn));  // open: preset, reset
endmodule

// CLK
module \十进制计数器  (
  input  LD,
  input  ENP,
  input  ENT,
  input  CLR,
  input  ENP_2,
  input  ENT_2,
  input  [3:0] in_7
);

  wire and_1_out, and_2_out, clk_2_out, clk_out, \n4位同步二进制计数器_2_rco , not_1_out, not_2_out, not_3_out,
       not_4_out, or_1_out;
  wire [3:0] \n4位同步二进制计数器_1_q , \n4位同步二进制计数器_2_q ;

  Clock clk (.out(clk_out));
  Clock clk_2 (.out(clk_2_out));
  \_4位同步二进制计数器  \u_4位同步二进制计数器_1  (
    .CLK(clk_out), .LD(LD), .CLR(and_1_out), .ENP(ENP), .ENT(ENT), .Q(\n4位同步二进制计数器_1_q [0]),
    .Q1(\n4位同步二进制计数器_1_q [1]), .Q2(\n4位同步二进制计数器_1_q [2]), .Q3(\n4位同步二进制计数器_1_q [3]));  // open: D0, D1, D2, D3, RCO
  or or_1 (or_1_out, and_2_out, \n4位同步二进制计数器_2_rco );
  \_4位同步二进制计数器  \u_4位同步二进制计数器_2  (
    .CLK(clk_2_out), .LD(or_1_out), .CLR(CLR), .D0(in_7[0]), .D1(in_7[1]), .D2(in_7[2]), .D3(in_7[3]),
    .ENP(ENP_2), .ENT(ENT_2), .Q(\n4位同步二进制计数器_2_q [0]), .Q1(\n4位同步二进制计数器_2_q [1]), .Q2(\n4位同步二进制计数器_2_q [2]),
    .Q3(\n4位同步二进制计数器_2_q [3]), .RCO(\n4位同步二进制计数器_2_rco ));
  not not_1 (not_1_out, \n4位同步二进制计数器_2_q [0]);
  not not_2 (not_2_out, \n4位同步二进制计数器_2_q [1]);
  and and_1 (and_1_out, \n4位同步二进制计数器_1_q [0], \n4位同步二进制计数器_1_q [3]);
  Hex_Digit_Display hex_digit_display_1 (.value(\n4位同步二进制计数器_2_q ));  // open: dp
  not not_3 (not_3_out, \n4位同步二进制计数器_2_q [3]);
  not not_4 (not_4_out, \n4位同步二进制计数器_2_q [2]);
  and and_2 (and_2_out, not_1_out, not_2_out, not_4_out, not_3_out);
  Hex_Digit_Display hex_digit_display_2 (.value(\n4位同步二进制计数器_1_q ));  // open: dp
  DotMatrix #(.matrixcols(1), .matrixrows(1)) dotmatrix_1 (.col0(and_1_out));
  DotMatrix #(.matrixcols(1), .matrixrows(1)) dotmatrix_2 (.col0(\n4位同步二进制计数器_2_rco ));
endmodule
