// Logisim project lab3.2.circ as structural Verilog: 2 circuits, main circuit 4位通用移位寄存器
module \_4位通用移位寄存器  (
  input  CLK,
  input  CLR,
  input  LIN,
  input  D,
  input  C,
  input  B,
  input  S1,
  input  S0,
  input  A,
  input  RIN,
  output QD,
  output QC,
  output QB,
  output QA
);

  wire _00_2_out, _00_3_out, _00_4_out, _00_out, _01_2_out, _01_3_out, _01_4_out, _01_out, _10_2_out,
       _10_3_out, _10_4_out, _10_out, _11_2_out, _11_3_out, _11_4_out, _11_out, not_1_out, not_2_out,
       not_3_out, not_4_out, not_5_out, not_6_out, or_1_out, or_2_out, or_3_out, or_4_out;

  not not_1 (not_1_out, S1);
  not not_2 (not_2_out, S0);
  not not_3 (not_3_out, CLK);
  not not_4 (not_4_out, CLR);
  not not_5 (not_5_out, not_1_out);
  not not_6 (not_6_out, not_2_out);
  and _10 (_10_out, not_4_out, LIN, not_5_out, not_2_out);
  and _00 (_00_out, not_4_out, QD, not_1_out, not_2_out);
  and _11 (_11_out, not_4_out, D, not_5_out, not_6_out);
  and _01 (_01_out, not_4_out, QC, not_1_out, not_6_out);
  and _10_2 (_10_2_out, not_4_out, QD, not_5_out, not_2_out);
  and _00_2 (_00_2_out, not_4_out, QC, not_1_out, not_2_out);
  and _11_2 (_11_2_out, not_4_out, C, not_5_out, not_6_out);
  and _01_2 (_01_2_out, not_4_out, QB, not_1_out, not_6_out);
  and _10_3 (_10_3_out, not_4_out, QC, not_5_out, not_2_out);
  and _00_3 (_00_3_out, not_4_out, QB, not_1_out, not_2_out);
  and _11_3 (_11_3_out, not_4_out, B, not_5_out, not_6_out);
  and _01_3 (_01_3_out, not_4_out, QA, not_1_out, not_6_out);
  and _10_4 (_10_4_out, not_4_out, QB, not_5_out, not_2_out);
  and _00_4 (_00_4_out, not_4_out, QA, not_1_out, not_2_out);
  and _11_4 (_11_4_out, not_4_out, A, not_5_out, not_6_out);
  and _01_4 (_01_4_out, not_4_out, RIN, not_1_out, not_6_out);
  or or_1 (or_1_out, _10_out, _00_out, _11_out, _01_out);
  or or_2 (or_2_out, _10_2_out, _00_2_out, _11_2_out, _01_2_out);
  or or_3 (or_3_out, _10_3_out, _00_3_out, _11_3_out, _01_3_out);
  or or_4 (or_4_out, _10_4_out, _00_4_out, _11_4_out, _01_4_out);
  D_Flip_Flop d_ff_1 (.clk(not_3_out), .D(or_1_out), .Q(QD));  // open: Qn, preset, reset
  D_Flip_Flop d_ff_2 (.clk(not_3_out), .D(or_2_out), .Q(QC));  // open: Qn, preset, reset
  D_Flip_Flop d_ff_3 (.clk(not_3_out), .D(or_3_out), .Q(QB));  // open: Qn, preset, reset
  D_Flip_Flop d_ff_4 (.clk(not_3_out), .D(or_4_out), .Q(QA));  // open: Qn, preset, reset
endmodule

module \演示  (
  input  CLR,
  input  D,
  input  C,
  input  B,
  input  A,
  input  S1,
  input  S0
);

  wire and_1_out, and_2_out, CLK_out, not_1_out, not_2_out, or_1_out;
  wire [3:0] \n4位通用移位寄存器_1_qd ;

  Clock CLK (.out(CLK_out));
  // Digital_Oscilloscope #(.nState(16)) digital_oscilloscope_1: pin names not known; wires that end beside it: CLK_out, \n4位通用移位寄存器_1_qd [2], \n4位通用移位寄存器_1_qd [3]
  \_4位通用移位寄存器  \u_4位通用移位寄存器_1  (
    .CLK(CLK_out), .CLR(CLR), .LIN(or_1_out), .D(D), .C(C), .B(B), .S1(S1), .S0(S0), .A(A),
    .QD(\n4位通用移位寄存器_1_qd [0]), .QC(\n4位通用移位寄存器_1_qd [1]), .QB(\n4位通用移位寄存器_1_qd [2]), .QA(\n4位通用移位寄存器_1_qd [3]));  // open: RIN
  not not_1 (not_1_out, \n4位通用移位寄存器_1_qd [3]);
  Hex_Digit_Display hex_digit_display_1 (.value(\n4位通用移位寄存器_1_qd ));  // open: dp
  not not_2 (not_2_out, \n4位通用移位寄存器_1_qd [2]);
  and and_1 (and_1_out, not_2_out, \n4位通用移位寄存器_1_qd [3]);
  and and_2 (and_2_out, \n4位通用移位寄存器_1_qd [2], not_1_out);
  or or_1 (or_1_out, and_1_out, and_2_out);
endmodule
