// Logisim project lab3.3.circ as structural Verilog: 3 circuits, main circuit 寄存器堆
module \寄存器堆  (
  input  [4:0] RA,
  input  [4:0] RW,
  input  [31:0] Din,
  input  [4:0] RB,
  input  WE,
  input  CLK,
  output [31:0] RDA,
  output [31:0] RDB
);

  wire and_1_out, and_2_out, and_3_out, and_4_out, and_5_out, and_6_out, and_7_out, and_8_out, and_9_out,
       and_10_out, and_11_out, and_12_out, and_13_out, and_14_out, and_15_out, and_16_out, and_17_out,
       and_18_out, and_19_out, and_20_out, and_21_out, and_22_out, and_23_out, and_24_out, and_25_out,
       and_26_out, and_27_out, and_28_out, and_29_out, and_30_out, and_31_out, and_32_out, decoder_1_out0,
       decoder_1_out1, decoder_1_out2, decoder_1_out3, decoder_1_out4, decoder_1_out5, decoder_1_out6,
       decoder_1_out7, decoder_1_out8, decoder_1_out9, decoder_1_out10, decoder_1_out11, decoder_1_out12,
       decoder_1_out13, decoder_1_out14, decoder_1_out15, decoder_1_out16, decoder_1_out17, decoder_1_out18,
       decoder_1_out19, decoder_1_out20, decoder_1_out21, decoder_1_out22, decoder_1_out23, decoder_1_out24,
       decoder_1_out25, decoder_1_out26, decoder_1_out27, decoder_1_out28, decoder_1_out29, decoder_1_out30,
       decoder_1_out31;
  wire [31:0] \寄存器_1_out_3 , \寄存器_2_out_3 , \寄存器_3_out_3 , \寄存器_4_out_3 , \寄存器_5_out_3 , \寄存器_6_out_3 ,
       \寄存器_7_out_3 , \寄存器_8_out_3 , \寄存器_9_out_3 , \寄存器_10_out_3 , \寄存器_11_out_3 , \寄存器_12_out_3 ,
       \寄存器_13_out_3 , \寄存器_14_out_3 , \寄存器_15_out_3 , \寄存器_16_out_3 , \寄存器_17_out_3 , \寄存器_18_out_3 ,
       \寄存器_19_out_3 , \寄存器_20_out_3 , \寄存器_22_out_3 , \寄存器_23_out_3 , \寄存器_24_out_3 , \寄存器_25_out_3 ,
       \寄存器_26_out_3 , \寄存器_27_out_3 , \寄存器_28_out_3 , \寄存器_29_out_3 , \寄存器_30_out_3 , \寄存器_31_out_3 ,
       \寄存器_32_out_3 ;

  Decoder #(.select(5), .enable("false")) decoder_1 (
    .out0(decoder_1_out0), .out1(decoder_1_out1), .out2(decoder_1_out2), .out3(decoder_1_out3),
    .out4(decoder_1_out4), .out5(decoder_1_out5), .out6(decoder_1_out6), .out7(decoder_1_out7),
    .out8(decoder_1_out8), .out9(decoder_1_out9), .out10(decoder_1_out10), .out11(decoder_1_out11),
    .out12(decoder_1_out12), .out13(decoder_1_out13), .out14(decoder_1_out14), .out15(decoder_1_out15),
    .out16(decoder_1_out16), .out17(decoder_1_out17), .out18(decoder_1_out18), .out19(decoder_1_out19),
    .out20(decoder_1_out20), .out21(decoder_1_out21), .out22(decoder_1_out22), .out23(decoder_1_out23),
    .out24(decoder_1_out24), .out25(decoder_1_out25), .out26(decoder_1_out26), .out27(decoder_1_out27),
    .out28(decoder_1_out28), .out29(decoder_1_out29), .out30(decoder_1_out30), .out31(decoder_1_out31),
    .sel(RW));
  and and_1 (and_1_out, WE, CLK, decoder_1_out0);
  and and_2 (and_2_out, WE, CLK, decoder_1_out1);
  and and_3 (and_3_out, WE, CLK, decoder_1_out2);
  and and_4 (and_4_out, WE, CLK, decoder_1_out3);
  and and_5 (and_5_out, WE, CLK, decoder_1_out4);
  and and_6 (and_6_out, WE, CLK, decoder_1_out5);
  and and_7 (and_7_out, WE, CLK, decoder_1_out6);
  and and_8 (and_8_out, WE, CLK, decoder_1_out7);
  and and_9 (and_9_out, WE, CLK, decoder_1_out8);
  and and_10 (and_10_out, WE, CLK, decoder_1_out9);
  and and_11 (and_11_out, WE, CLK, decoder_1_out10);
  and and_12 (and_12_out, WE, CLK, decoder_1_out11);
  and and_13 (and_13_out, WE, CLK, decoder_1_out12);
  and and_14 (and_14_out, WE, CLK, decoder_1_out13);
  and and_15 (and_15_out, WE, CLK, decoder_1_out14);
  and and_16 (and_16_out, WE, CLK, decoder_1_out15);
  and and_17 (and_17_out, WE, CLK, decoder_1_out16);
  and and_18 (and_18_out, WE, CLK, decoder_1_out17);
  and and_19 (and_19_out, WE, CLK, decoder_1_out18);
  and and_20 (and_20_out, WE, CLK, decoder_1_out19);
  and and_21 (and_21_out, WE, CLK, decoder_1_out20);
  and and_22 (and_22_out, WE, CLK, decoder_1_out21);
  and and_23 (and_23_out, WE, CLK, decoder_1_out22);
  and and_24 (and_24_out, WE, CLK, decoder_1_out23);
  and and_25 (and_25_out, WE, CLK, decoder_1_out24);
  and and_26 (and_26_out, WE, CLK, decoder_1_out25);
  and and_27 (and_27_out, WE, CLK, decoder_1_out26);
  and and_28 (and_28_out, WE, CLK, decoder_1_out27);
  and and_29 (and_29_out, WE, CLK, decoder_1_out28);
  and and_30 (and_30_out, WE, CLK, decoder_1_out29);
  and and_31 (and_31_out, WE, CLK, decoder_1_out30);
  and and_32 (and_32_out, WE, CLK, decoder_1_out31);
  \寄存器  \u_寄存器_1  (.D(Din), .CLK(and_1_out), .out_3(\寄存器_1_out_3 ));
  \寄存器  \u_寄存器_2  (.D(Din), .CLK(and_2_out), .out_3(\寄存器_2_out_3 ));
  \寄存器  \u_寄存器_3  (.D(Din), .CLK(and_3_out), .out_3(\寄存器_3_out_3 ));
  \寄存器  \u_寄存器_4  (.D(Din), .CLK(and_4_out), .out_3(\寄存器_4_out_3 ));
  \寄存器  \u_寄存器_5  (.D(Din), .CLK(and_5_out), .out_3(\寄存器_5_out_3 ));
  \寄存器  \u_寄存器_6  (.D(Din), .CLK(and_6_out), .out_3(\寄存器_6_out_3 ));
  \寄存器  \u_寄存器_7  (.D(Din), .CLK(and_7_out), .out_3(\寄存器_7_out_3 ));
  \寄存器  \u_寄存器_8  (.D(Din), .CLK(and_8_out), .out_3(\寄存器_8_out_3 ));
  \寄存器  \u_寄存器_9  (.D(Din), .CLK(and_9_out), .out_3(\寄存器_9_out_3 ));
  \寄存器  \u_寄存器_10  (.D(Din), .CLK(and_10_out), .out_3(\寄存器_10_out_3 ));
  \寄存器  \u_寄存器_11  (.D(Din), .CLK(and_11_out), .out_3(\寄存器_11_out_3 ));
  \寄存器  \u_寄存器_12  (.D(Din), .CLK(and_12_out), .out_3(\寄存器_12_out_3 ));
  \寄存器  \u_寄存器_13  (.D(Din), .CLK(and_13_out), .out_3(\寄存器_13_out_3 ));
  \寄存器  \u_寄存器_14  (.D(Din), .CLK(and_14_out), .out_3(\寄存器_14_out_3 ));
  \寄存器  \u_寄存器_15  (.D(Din), .CLK(and_15_out), .out_3(\寄存器_15_out_3 ));
  \寄存器  \u_寄存器_16  (.D(Din), .CLK(and_16_out), .out_3(\寄存器_16_out_3 ));
  \寄存器  \u_寄存器_17  (.D(Din), .CLK(and_17_out), .out_3(\寄存器_17_out_3 ));
  \寄存器  \u_寄存器_18  (.D(Din), .CLK(and_18_out), .out_3(\寄存器_18_out_3 ));
  \寄存器  \u_寄存器_19  (.D(Din), .CLK(and_19_out), .out_3(\寄存器_19_out_3 ));
  \寄存器  \u_寄存器_20  (.D(Din), .CLK(and_20_out), .out_3(\寄存器_20_out_3 ));
  \寄存器  \u_寄存器_21  (.D(Din), .CLK(and_21_out), .out_3(\寄存器_20_out_3 ));
  \寄存器  \u_寄存器_22  (.D(Din), .CLK(and_22_out), .out_3(\寄存器_22_out_3 ));
  \寄存器  \u_寄存器_23  (.D(Din), .CLK(and_23_out), .out_3(\寄存器_23_out_3 ));
  \寄存器  \u_寄存器_24  (.D(Din), .CLK(and_24_out), .out_3(\寄存器_24_out_3 ));
  \寄存器  \u_寄存器_25  (.D(Din), .CLK(and_25_out), .out_3(\寄存器_25_out_3 ));
  \寄存器  \u_寄存器_26  (.D(Din), .CLK(and_26_out), .out_3(\寄存器_26_out_3 ));
  \寄存器  \u_寄存器_27  (.D(Din), .CLK(and_27_out), .out_3(\寄存器_27_out_3 ));
  \寄存器  \u_寄存器_28  (.D(Din), .CLK(and_28_out), .out_3(\寄存器_28_out_3 ));
  \寄存器  \u_寄存器_29  (.D(Din), .CLK(and_29_out), .out_3(\寄存器_29_out_3 ));
  \寄存器  \u_寄存器_30  (.D(Din), .CLK(and_30_out), .out_3(\寄存器_30_out_3 ));
  \寄存器  \u_寄存器_31  (.D(Din), .CLK(and_31_out), .out_3(\寄存器_31_out_3 ));
  \寄存器  \u_寄存器_32  (.D(Din), .CLK(and_32_out), .out_3(\寄存器_32_out_3 ));
  Multiplexer #(.select(5), .width(32), .enable("false")) multiplexer_1 (
    .in0(\寄存器_1_out_3 ), .in1(\寄存器_2_out_3 ), .in2(\寄存器_3_out_3 ), .in3(\寄存器_4_out_3 ), .in4(\寄存器_5_out_3 ),
    .in5(\寄存器_6_out_3 ), .in6(\寄存器_7_out_3 ), .in7(\寄存器_8_out_3 ), .in8(\寄存器_9_out_3 ), .in9(\寄存器_10_out_3 ),
    .in10(\寄存器_11_out_3 ), .in11(\寄存器_12_out_3 ), .in12(\寄存器_13_out_3 ), .in13(\寄存器_14_out_3 ),
    .in14(\寄存器_15_out_3 ), .in15(\寄存器_16_out_3 ), .in16(\寄存器_17_out_3 ), .in17(\寄存器_18_out_3 ),
    .in18(\寄存器_19_out_3 ), .in19(\寄存器_20_out_3 ), .in20(\寄存器_20_out_3 ), .in21(\寄存器_22_out_3 ),
    .in22(\寄存器_23_out_3 ), .in23(\寄存器_24_out_3 ), .in24(\寄存器_25_out_3 ), .in25(\寄存器_26_out_3 ),
    .in26(\寄存器_27_out_3 ), .in27(\寄存器_28_out_3 ), .in28(\寄存器_29_out_3 ), .in29(\寄存器_30_out_3 ),
    .in30(\寄存器_31_out_3 ), .in31(\寄存器_32_out_3 ), .out(RDA), .sel(RA));
  Multiplexer #(.select(5), .width(32), .enable("false")) multiplexer_2 (
    .in0(\寄存器_1_out_3 ), .in1(\寄存器_2_out_3 ), .in2(\寄存器_3_out_3 ), .in3(\寄存器_4_out_3 ), .in4(\寄存器_5_out_3 ),
    .in5(\寄存器_6_out_3 ), .in6(\寄存器_7_out_3 ), .in7(\寄存器_8_out_3 ), .in8(\寄存器_9_out_3 ), .in9(\寄存器_10_out_3 ),
    .in10(\寄存器_11_out_3 ), .in11(\寄存器_12_out_3 ), .in12(\寄存器_13_out_3 ), .in13(\寄存器_14_out_3 ),
    .in14(\寄存器_15_out_3 ), .in15(\寄存器_16_out_3 ), .in16(\寄存器_17_out_3 ), .in17(\寄存器_18_out_3 ),
    .in18(\寄存器_19_out_3 ), .in19(\寄存器_20_out_3 ), .in20(\寄存器_20_out_3 ), .in21(\寄存器_22_out_3 ),
    .in22(\寄存器_23_out_3 ), .in23(\寄存器_24_out_3 ), .in24(\寄存器_25_out_3 ), .in25(\寄存器_26_out_3 ),
    .in26(\寄存器_27_out_3 ), .in27(\寄存器_28_out_3 ), .in28(\寄存器_29_out_3 ), .in29(\寄存器_30_out_3 ),
    .in30(\寄存器_31_out_3 ), .in31(\寄存器_32_out_3 ), .out(RDB), .sel(RB));
endmodule

module \寄存器  (
  input  [31:0] D,
  input  CLK,
  output [31:0] out_3
);

  Register #(.width(32), .Select("low")) register_1 (.D(D), .Q(out_3), .clk(CLK));  // open: en, clr
endmodule

module \演示  (
  input  [4:0] RA,
  input  [4:0] RB,
  input  Write_Enable,
  input  [4:0] RW,
  input  [31:0] Din,
  output [31:0] RDA,
  output [31:0] RDB
);

  wire clock_1_out;

  Clock clock_1 (.out(clock_1_out));
  \寄存器堆  \u_寄存器堆_1  (.RA(RA), .Din(Din), .RB(RB), .WE(Write_Enable), .CLK(clock_1_out), .RW(RW), .RDA(RDA), .RDB(RDB));
endmodule
