// Logisim project 4位串行进位加法器.circ as structural Verilog: 2 circuits, main circuit 全加器
module main (
  input  in_1,
  input  in_2,
  input  in_3,
  input  in_4,
  input  in_5,
  input  in_6,
  input  in_7,
  input  in_8,
  input  in_9,
  output out_10
);

  wire \全加器_2_cout , \全加器_3_cout , \全加器_4_cout ;
  wire [3:0] \全加器_4_f ;

  Hex_Digit_Display hex_digit_display_1 (.value({in_1, in_3, in_5, in_7}), .dp(1'b1));
  Hex_Digit_Display hex_digit_display_2 (.value({in_2, in_4, in_6, in_8}), .dp(1'b1));
  \全加器  \u_全加器_1  (.A(in_1), .B(in_2), .COUT(out_10), .F(\全加器_4_f [3]), .CIN(\全加器_2_cout ));
  \全加器  \u_全加器_2  (.A(in_3), .B(in_4), .COUT(\全加器_2_cout ), .F(\全加器_4_f [2]), .CIN(\全加器_3_cout ));
  \全加器  \u_全加器_3  (.A(in_5), .B(in_6), .COUT(\全加器_3_cout ), .F(\全加器_4_f [1]), .CIN(\全加器_4_cout ));
  \全加器  \u_全加器_4  (.A(in_7), .B(in_8), .COUT(\全加器_4_cout ), .F(\全加器_4_f [0]), .CIN(in_9));
  Hex_Digit_Display hex_digit_display_3 (.value(\全加器_4_f ), .dp(1'b1));
endmodule

module \全加器  (
  input  A,
  input  B,
  input  CIN,
  output COUT,
  output F
);

  wire and_1_out, and_2_out, and_3_out;

  and and_1 (and_1_out, A, B);
  and and_2 (and_2_out, B, CIN);
  and and_3 (and_3_out, A, CIN);
  or or_1 (COUT, and_1_out, and_2_out, and_3_out);
  ExactlyOne xor_1 (.out(F), .in0(A), .in1(B), .in2(CIN));
endmodule
