// Logisim project 8-3优先级编码器.circ as structural Verilog: 1 circuit, main circuit main
module main (
  input  in_1,
  input  in_2,
  input  in_3,
  input  in_4,
  input  in_5,
  input  in_6,
  input  in_7,
  input  in_8
);

  wire and_1_out, and_2_out, and_3_out, and_4_out, and_5_out, and_6_out, and_7_out, not_1_out, not_2_out,
       not_3_out, not_4_out, not_5_out, not_6_out, not_7_out, not_8_out, not_9_out, not_10_out, not_11_out,
       not_12_out, not_13_out, not_14_out, not_15_out, not_16_out, not_17_out, not_18_out, not_19_out,
       not_20_out, not_21_out, not_22_out, not_23_out, not_24_out, not_25_out, not_26_out, not_27_out,
       not_28_out;
  wire [2:0] or_3_out;

  and and_1 (and_1_out, not_1_out, in_2);
  not not_1 (not_1_out, in_1);
  and and_2 (and_2_out, not_3_out, not_2_out, in_3);
  not not_2 (not_2_out, in_2);
  not not_3 (not_3_out, in_1);
  and and_3 (and_3_out, not_5_out, not_4_out, not_6_out, in_4);
  not not_4 (not_4_out, in_2);
  not not_5 (not_5_out, in_1);
  not not_6 (not_6_out, in_3);
  and and_4 (and_4_out, not_10_out, not_8_out, not_7_out, not_9_out, in_5);
  not not_7 (not_7_out, in_3);
  not not_8 (not_8_out, in_2);
  not not_9 (not_9_out, in_4);
  not not_10 (not_10_out, in_1);
  or or_1 (or_3_out[2], and_5_out, and_6_out, and_4_out, and_7_out);
  and and_5 (and_5_out, not_12_out, not_14_out, not_13_out, not_15_out, not_11_out, in_6);
  not not_11 (not_11_out, in_5);
  not not_12 (not_12_out, in_1);
  not not_13 (not_13_out, in_3);
  not not_14 (not_14_out, in_2);
  not not_15 (not_15_out, in_4);
  Hex_Digit_Display hex_digit_display_1 (.value({1'b0, or_3_out}), .dp(1'b1));
  or or_2 (or_3_out[1], and_6_out, and_2_out, and_3_out, and_7_out);
  and and_6 (and_6_out, not_20_out, not_18_out, not_17_out, not_21_out, not_19_out, not_16_out, in_7);
  not not_16 (not_16_out, in_6);
  not not_17 (not_17_out, in_3);
  not not_18 (not_18_out, in_2);
  not not_19 (not_19_out, in_5);
  not not_20 (not_20_out, in_1);
  not not_21 (not_21_out, in_4);
  and and_7 (and_7_out, not_23_out, not_24_out, not_22_out, not_25_out, not_27_out, not_28_out, not_26_out, in_8);
  not not_22 (not_22_out, in_3);
  not not_23 (not_23_out, in_1);
  not not_24 (not_24_out, in_2);
  not not_25 (not_25_out, in_4);
  or or_3 (or_3_out[0], and_1_out, and_3_out, and_5_out, and_7_out);
  not not_26 (not_26_out, in_7);
  not not_27 (not_27_out, in_5);
  not not_28 (not_28_out, in_6);

  // Notes on the sheet:
  //   I0
  //   8-3 优先级编码器
  //   I2
  //   I1
  //   I3
  //   O 0
  //   I4
  //   I5
  //   O 1
  //   I6
  //   0 2
  //   I7
endmodule
