// Logisim project ALU电路.circ as structural Verilog: 3 circuits, main circuit main
module main (
  input  A,
  input  B,
  input  in_3,
  input  in_4,
  input  in_5,
  output F
);

  wire and_1_out, not_1_out, not_2_out, or_1_out, part_1_f, part_2_f, xnor_1_out;

  circuit part_1 (.A(A), .B(B), .F(part_1_f));  // open: COUT
  circuit_2 part_2 (.A(A), .B(B), .F(part_2_f));  // open: 借位
  and and_1 (and_1_out, A, B);
  or or_1 (or_1_out, A, B);
  xnor xnor_1 (xnor_1_out, A, B);
  not not_1 (not_1_out, A);
  not not_2 (not_2_out, B);
  Multiplexer #(.select(3), .enable("false")) multiplexer_1 (
    .in0(part_1_f), .in1(part_2_f), .in2(and_1_out), .in3(or_1_out), .in4(xnor_1_out), .in5(not_1_out),
    .in6(A), .in7(not_2_out), .out(F), .sel({in_3, in_4, in_5}));
endmodule

module circuit (
  input  A,
  input  B,
  output COUT,
  output F
);

  wire and_1_out, and_2_out, and_3_out;

  and and_1 (and_1_out, A, B);
  and and_2 (and_2_out, B, 1'b0);
  and and_3 (and_3_out, A, 1'b0);
  or or_1 (COUT, and_1_out, and_2_out, and_3_out);
  ExactlyOne xor_1 (.out(F), .in0(A), .in1(B), .in2(1'b0));
endmodule

module circuit_2 (
  input  A,
  input  B,
  output F,
  output \借位 
);

  wire not_1_out;

  not not_1 (not_1_out, A);
  xor xor_1 (F, A, B);
  and and_1 (\借位 , B, not_1_out);
endmodule
