// Logisim project LED显示NJUCS.circ as structural Verilog: 1 circuit, main circuit main
module main (
  input  [6:0] in_1,
  input  [6:0] in_2,
  input  [6:0] in_3,
  input  [6:0] in_4,
  input  [6:0] in_5,
  input  [6:0] in_6,
  input  [6:0] in_7,
  input  [6:0] in_8,
  input  [6:0] in_9,
  input  [6:0] in_10,
  input  [6:0] in_11,
  input  [6:0] in_12,
  input  [6:0] in_13,
  input  [6:0] in_14,
  input  [6:0] in_15,
  input  [6:0] in_16,
  input  [6:0] in_17,
  input  [6:0] in_18,
  input  [6:0] in_19,
  input  [6:0] in_20,
  input  [6:0] in_21,
  input  [6:0] in_22,
  input  [6:0] in_23,
  input  [6:0] in_24,
  input  [6:0] in_25,
  input  [6:0] in_26,
  input  [6:0] in_27,
  input  [6:0] in_28,
  input  [6:0] in_29,
  input  [6:0] in_30,
  input  [6:0] in_31,
  input  [6:0] in_32,
  input  [6:0] in_33,
  input  [6:0] in_34,
  input  [6:0] in_35
);

  DotMatrix #(.matrixcols(7)) dotmatrix_1 (
    .col0(in_1), .col1(in_3), .col2(in_5), .col3(in_7), .col4(in_9), .col5(in_11), .col6(in_13));
  DotMatrix #(.matrixcols(7)) dotmatrix_2 (
    .col0(in_15), .col1(in_17), .col2(in_17), .col3(in_21), .col4(in_23), .col5(in_25), .col6(in_27));
  DotMatrix #(.matrixcols(7)) dotmatrix_3 (
    .col0(in_28), .col1(in_26), .col2(in_24), .col3(in_22), .col4(in_20), .col5(in_18), .col6(in_16));
  DotMatrix #(.matrixcols(7)) dotmatrix_4 (
    .col0(in_29), .col1(in_30), .col2(in_31), .col3(in_32), .col4(in_33), .col5(in_34), .col6(in_35));
  DotMatrix #(.matrixcols(7)) dotmatrix_5 (
    .col0(in_14), .col1(in_12), .col2(in_10), .col3(in_8), .col4(in_6), .col5(in_4), .col6(in_2));

  assign in_19 = in_17;
endmodule
