// Logisim project lab5.1.circ as structural Verilog: 3 circuits, main circuit main
module main (
  input  [11:0] \地址数据 ,
  input  [31:0] \输入数据 ,
  input  \输入使能 ,
  input  \片选 ,
  input  \输出使能 ,
  output [31:0] \输出数据 
);

  wire \复位按钮_out , \时钟信号_out ;

  // Probe on \输入数据 
  Clock \u_时钟信号  (.out(\时钟信号_out ));
  Button \u_复位按钮  (.out(\复位按钮_out ));
  RAM #(.addrWidth(12), .dataWidth(32), .bus("separate"), .Select("low")) \RAM_输入输出分离同步模式  (
    .addr(\地址数据 ), .din(\输入数据 ), .data(\输出数据 ), .str(\输入使能 ), .sel(\片选 ), .clk(\时钟信号_out ), .ld(\输出使能 ),
    .clr(\复位按钮_out ));
  // Probe on \输出数据 
endmodule

module lab5_1_2 (
  input  [31:0] \输入数据 ,
  input  [11:0] \地址数据 ,
  input  \片选 ,
  input  \写使能 ,
  output [31:0] \输出数据 
);

  wire not_1_out, \复位按钮_out , \时钟信号_out ;

  Clock \u_时钟信号  (.out(\时钟信号_out ));
  Button \u_复位按钮  (.out(\复位按钮_out ));
  // Probe on \输入数据 
  assign \输出数据  = \写使能  ? \输入数据  : 32'bz;  // Controlled_Buffer controlled_buffer_1
  not not_1 (not_1_out, \写使能 );
  RAM #(.addrWidth(12), .dataWidth(32), .Select("low")) \RAM_同步模式  (
    .addr(\地址数据 ), .data(\输出数据 ), .sel(\片选 ), .clk(\时钟信号_out ), .ld(not_1_out), .clr(\复位按钮_out ));
  // Probe on \输出数据 
endmodule

module lab5_1_3 (
  input  [31:0] \输入数据 ,
  input  [11:0] \地址数据 ,
  input  \片选 ,
  input  \写使能 ,
  output [31:0] \输出数据 
);

  wire not_1_out, \复位按钮_out ;

  // Probe on \输入数据 
  Button \u_复位按钮  (.out(\复位按钮_out ));
  assign \输出数据  = \写使能  ? \输入数据  : 32'bz;  // Controlled_Buffer controlled_buffer_1
  not not_1 (not_1_out, \写使能 );
  RAM #(.addrWidth(12), .dataWidth(32), .bus("asynch"), .Select("low")) \RAM_异步模式  (
    .addr(\地址数据 ), .data(\输出数据 ), .sel(\片选 ), .ld(not_1_out), .clr(\复位按钮_out ));
  // Probe on \输出数据 
endmodule
