// Logisim project lab5.2.circ as structural Verilog: 2 circuits, main circuit main
module main (
  input  [31:0] imm,
  input  [2:0] extop,
  input  in_3,
  input  in_4,
  input  in_5,
  output [31:0] instr,
  output [6:0] op,
  output [4:0] rd,
  output [2:0] funct3,
  output [4:0] Rs1,
  output [4:0] Rs2,
  output [6:0] funct7,
  output [31:0] imm_2
);

  wire and_1_out, button_1_out, Clock, or_1_out;
  wire [31:0] adder_1_out, multiplexer_1_out, PC_q;

  Register #(.width(32), .Select("low")) PC (.D(adder_1_out), .en(1'b1), .Q(PC_q), .clk(Clock), .clr(button_1_out));
  Button button_1 (.out(button_1_out));
  Clock clock_1 (.out(Clock));
  Multiplexer #(.width(32), .enable("false")) multiplexer_1 (
    .in0(32'h4), .in1(imm), .out(multiplexer_1_out), .sel(or_1_out));
  or or_1 (or_1_out, in_3, and_1_out);
  and and_1 (and_1_out, in_4, in_5);
  Adder #(.width(32)) adder_1 (.a(PC_q), .b(multiplexer_1_out), .out(adder_1_out));  // open: cin, cout
  RAM #(.addrWidth(10), .dataWidth(32), .bus("asynch"), .Select("low")) \u_指令寄存器RAM  (
    .addr(PC_q[9:0]), .data({funct7, instr[24:15], funct3, instr[11:0]}));  // open: sel, ld, clr
  lab5_2_2 lab5_2_2_1 (.instr({funct7, instr[24:15], funct3, instr[11:0]}), .extop(extop), .imm(imm_2));

  assign {instr[31:25], instr[14:12]} = {funct7, funct3};
  assign op = instr[6:0];
  assign rd = instr[11:7];
  assign Rs1 = instr[19:15];
  assign Rs2 = instr[24:20];

  // Other names for the same wires on the sheet: Branch = in_4; Jump = in_3; Zero = in_5
endmodule

module lab5_2_2 (
  input  [31:0] instr,
  input  [2:0] extop,
  output [31:0] imm
);

  wire [11:0] bit_extender_4_out;
  wire [19:0] bit_extender_1_out, bit_extender_2_out, bit_extender_3_out;

  assign bit_extender_1_out = {{19{instr[31]}}, instr[31]};  // Bit_Extender bit_extender_1
  assign bit_extender_2_out = {{19{instr[31]}}, instr[31]};  // Bit_Extender bit_extender_2
  assign bit_extender_3_out = {{19{instr[31]}}, instr[31]};  // Bit_Extender bit_extender_3
  assign bit_extender_4_out = {{11{instr[31]}}, instr[31]};  // Bit_Extender bit_extender_4
  Multiplexer #(.select(3), .width(32), .enable("false")) multiplexer_1 (
    .in0({bit_extender_1_out, instr[31:20]}), .in1({instr[31:12], {12{1'b0}}}),
    .in2({bit_extender_2_out, instr[31:25], instr[11:7]}),
    .in3({bit_extender_3_out, instr[7], instr[30:25], instr[11:8], 1'b1}),
    .in4({bit_extender_4_out, instr[19:12], instr[20], instr[30:21], 1'b1}), .in5({32{1'b0}}),
    .in6({32{1'b0}}), .in7({32{1'b0}}), .out(imm), .sel(extop));
endmodule
