// Logisim project lab5.3.circ as structural Verilog: 2 circuits, main circuit main
module main (
  input  [6:0] in_1,
  input  fn_2,
  input  fn_1,
  input  fn_0,
  output RegWr,
  output MemtoReg,
  output MemWr,
  output Branch,
  output Jump,
  output ALUctr_3,
  output ALUctr_2,
  output ALUctr_1,
  output ALUctr_0
);

  wire and_1_out, and_2_out, and_3_out, \I型_ALU_out , lui_out, or_1_out, \R型_out ;

  and \R型  (\R型_out , ~in_1[6], in_1[5], in_1[4], ~in_1[3], ~in_1[2], in_1[1], in_1[0]);  // AND_Gate
  and \I型_ALU  (\I型_ALU_out , ~in_1[6], ~in_1[5], in_1[4], ~in_1[3], ~in_1[2], in_1[1], in_1[0]);  // AND_Gate
  or or_1 (or_1_out, \R型_out , \I型_ALU_out );
  and lui (lui_out, ~in_1[6], in_1[5], in_1[4], ~in_1[3], in_1[2], in_1[1], in_1[0]);  // AND_Gate
  and and_1 (and_1_out, or_1_out, fn_2);
  and and_2 (and_2_out, or_1_out, fn_1);
  and and_3 (and_3_out, or_1_out, fn_0);
  and Load (MemtoReg, ~in_1[6], ~in_1[5], ~in_1[4], ~in_1[3], ~in_1[2], in_1[1], in_1[0]);  // AND_Gate
  and Store (MemWr, ~in_1[6], in_1[5], ~in_1[4], ~in_1[3], ~in_1[2], in_1[1], in_1[0]);  // AND_Gate
  and \B型  (Branch, in_1[6], in_1[5], ~in_1[4], ~in_1[3], ~in_1[2], in_1[1], in_1[0]);  // AND_Gate
  and \J型  (Jump, in_1[6], in_1[5], ~in_1[4], in_1[3], in_1[2], in_1[1], in_1[0]);  // AND_Gate
  or or_2 (ALUctr_3, lui_out, Branch);
  or or_3 (ALUctr_2, lui_out, and_1_out);
  or or_4 (ALUctr_1, lui_out, and_2_out);
  or or_5 (ALUctr_0, lui_out, and_3_out);
  or or_6 (RegWr, \R型_out , \I型_ALU_out , lui_out, MemtoReg);
endmodule

module _5_3_1 (
  input  func31,
  input  func32,
  input  func33,
  input  op1,
  input  op2,
  input  op3,
  input  op4,
  input  op5,
  input  op6,
  input  op7,
  output Branch,
  output Jump,
  output ALUASrc,
  output ALUBSrc0,
  output ALUBSrc1,
  output ALUctr0,
  output ALUctr1,
  output ALUctr2,
  output ALUctr3,
  output MemtoReg,
  output RegWr,
  output MemWr,
  output ExtOp0,
  output ExtOp1,
  output ExtOp2
);

  wire and_1_out, and_2_out, and_3_out, and_4_out, and_5_out, and_6_out, and_7_out, and_8_out, and_9_out,
       and_10_out, and_11_out, and_12_out, and_15_out, and_16_out, not_1_out, not_2_out, not_3_out,
       not_4_out, not_5_out, not_6_out, not_7_out, not_8_out, not_9_out, not_10_out, not_11_out, not_12_out,
       not_13_out, not_14_out, not_15_out, not_16_out, not_17_out, not_18_out, not_19_out, not_20_out,
       not_21_out, not_22_out;

  not not_1 (not_1_out, op1);
  not not_2 (not_2_out, op4);
  not not_3 (not_3_out, op1);
  not not_4 (not_4_out, op3);
  not not_5 (not_5_out, op4);
  not not_6 (not_6_out, op4);
  not not_7 (not_7_out, op4);
  not not_8 (not_8_out, op4);
  not not_9 (not_9_out, op4);
  not not_10 (not_10_out, op4);
  not not_11 (not_11_out, op4);
  not not_12 (not_12_out, op4);
  not not_13 (not_13_out, op3);
  not not_14 (not_14_out, op4);
  not not_15 (not_15_out, op2);
  not not_16 (not_16_out, op1);
  not not_17 (not_17_out, op3);
  not not_18 (not_18_out, func32);
  not not_19 (not_19_out, op4);
  not not_20 (not_20_out, op4);
  not not_21 (not_21_out, op5);
  and and_1 (and_1_out, not_1_out, op4);
  and and_2 (and_2_out, op1, not_2_out);
  and and_3 (and_3_out, not_3_out, not_4_out);
  not not_22 (not_22_out, op2);
  and and_4 (and_4_out, not_5_out, op5);
  and and_5 (and_5_out, not_6_out, op5);
  and and_6 (and_6_out, func33, not_7_out);
  and and_7 (and_7_out, not_8_out, op5);
  and and_8 (and_8_out, func32, op3);
  and and_9 (and_9_out, not_9_out, op5);
  and and_10 (and_10_out, func31, not_10_out);
  and and_11 (and_11_out, not_11_out, op5);
  and and_12 (and_12_out, op1, not_12_out);
  and and_13 (MemtoReg, not_13_out, not_14_out);
  or or_1 (RegWr, not_15_out, op4, op3);
  and and_14 (MemWr, not_16_out, op2, not_17_out);
  and and_15 (and_15_out, not_18_out, not_19_out);
  and and_16 (and_16_out, not_20_out, op5);
  and and_17 (ExtOp1, op2, not_21_out);
  or or_2 (Branch, and_1_out, and_2_out);
  or or_3 (ALUBSrc1, and_3_out, not_22_out, and_4_out);
  or or_4 (ALUctr0, and_5_out, and_6_out);
  or or_5 (ALUctr1, and_7_out, and_8_out);
  or or_6 (ALUctr2, and_9_out, and_10_out);
  or or_7 (ALUctr3, and_11_out, and_12_out);
  or or_8 (ExtOp0, and_15_out, and_16_out);

  assign ALUASrc = op4;
  assign ALUBSrc0 = op4;
  assign ExtOp2 = op4;
  assign Jump = op4;
endmodule
