// Logisim project Lab 6.circ as structural Verilog: 11 circuits, main circuit CPU
module CLA (
  input  B3,
  input  A3,
  input  B2,
  input  A2,
  input  B1,
  input  A1,
  input  B0,
  input  A0,
  input  C0,
  output C4,
  output S3,
  output S2,
  output S1,
  output S0,
  output Pg,
  output Gg
);

  wire and_1_out, and_2_out, and_4_out, and_5_out, and_6_out, and_7_out, and_8_out, and_10_out, and_11_out,
       and_12_out, nand_1_out, nand_2_out, nand_3_out, nand_4_out, nor_1_out, nor_2_out, nor_3_out,
       nor_4_out, not_1_out, not_2_out, not_3_out, not_4_out, not_5_out, not_6_out, or_1_out, or_2_out,
       or_3_out, or_4_out, or_5_out, or_6_out, or_7_out, or_8_out, or_9_out, or_10_out;

  not not_1 (not_1_out, C0);
  nand nand_1 (nand_1_out, B3, A3);
  nor nor_1 (nor_1_out, B3, A3);
  nand nand_2 (nand_2_out, B2, A2);
  nor nor_2 (nor_2_out, B2, A2);
  nand nand_3 (nand_3_out, B1, A1);
  nor nor_3 (nor_3_out, B1, A1);
  nand nand_4 (nand_4_out, B0, A0);
  nor nor_4 (nor_4_out, B0, A0);
  not not_2 (not_2_out, nor_1_out);
  or or_1 (or_1_out, ~nor_2_out, ~nand_1_out);  // OR_Gate
  or or_2 (or_2_out, ~nor_3_out, ~nand_1_out, ~nand_2_out);  // OR_Gate
  or or_3 (or_3_out, ~nor_4_out, ~nand_1_out, ~nand_2_out, ~nand_3_out);  // OR_Gate
  or or_4 (or_4_out, ~nand_1_out, ~nand_2_out, ~nand_3_out, ~nand_4_out, ~not_1_out);  // OR_Gate
  and and_1 (and_1_out, nand_1_out, ~nor_1_out);  // AND_Gate
  not not_3 (not_3_out, nor_2_out);
  or or_5 (or_5_out, ~nor_3_out, ~nand_2_out);  // OR_Gate
  or or_6 (or_6_out, ~nor_4_out, ~nand_2_out, ~nand_3_out);  // OR_Gate
  or or_7 (or_7_out, ~nand_2_out, ~nand_3_out, ~nand_4_out, ~not_1_out);  // OR_Gate
  and and_2 (and_2_out, nand_2_out, ~nor_2_out);  // AND_Gate
  not not_4 (not_4_out, nor_3_out);
  or or_8 (or_8_out, ~nor_4_out, ~nand_3_out);  // OR_Gate
  or or_9 (or_9_out, ~nand_3_out, ~nand_4_out, ~not_1_out);  // OR_Gate
  not not_5 (not_5_out, nor_4_out);
  and and_3 (C4, not_2_out, or_1_out, or_2_out, or_3_out, or_4_out);
  and and_4 (and_4_out, not_3_out, or_5_out, or_6_out, or_7_out);
  and and_5 (and_5_out, not_4_out, or_8_out, or_9_out);
  and and_6 (and_6_out, nand_3_out, ~nor_3_out);  // AND_Gate
  and and_7 (and_7_out, not_5_out, or_10_out);
  or or_10 (or_10_out, ~nand_4_out, ~not_1_out);  // OR_Gate
  and and_8 (and_8_out, nand_4_out, ~nor_4_out);  // AND_Gate
  not not_6 (not_6_out, not_1_out);
  and and_9 (Pg, ~nor_1_out, ~nor_2_out, ~nor_3_out, ~nor_4_out);  // AND_Gate
  and and_10 (and_10_out, ~nor_1_out, ~nand_2_out);  // AND_Gate
  and and_11 (and_11_out, ~nor_1_out, ~nor_2_out, ~nand_3_out);  // AND_Gate
  and and_12 (and_12_out, ~nor_1_out, ~nor_2_out, ~nor_3_out, nand_4_out);  // AND_Gate
  xor xor_1 (S3, and_1_out, and_4_out);
  xor xor_2 (S2, and_2_out, and_5_out);
  xor xor_3 (S1, and_6_out, and_7_out);
  xor xor_4 (S0, and_8_out, not_6_out);
  or or_11 (Gg, ~nand_1_out, and_10_out, and_11_out, and_12_out);  // OR_Gate
endmodule

module CLU (
  input  C0,
  input  G3,
  input  P3,
  input  G2,
  input  P2,
  input  G1,
  input  P1,
  input  G0,
  input  P0,
  output Gs,
  output C3,
  output C2,
  output C1,
  output Ps,
  output C4
);

  wire and_1_out, and_2_out, and_3_out, and_5_out, and_6_out, and_7_out, and_8_out, and_9_out, and_10_out,
       and_11_out, and_12_out, and_13_out, and_14_out;

  or or_1 (Gs, and_1_out, and_2_out, and_3_out, G3);
  and and_1 (and_1_out, P3, P2, P1, G0);
  and and_2 (and_2_out, G1, P2, P3);
  and and_3 (and_3_out, G2, P3);
  and and_4 (Ps, P3, P2, P1, P0);
  and and_5 (and_5_out, P3, G2);
  and and_6 (and_6_out, P3, P2, G1);
  or or_2 (C4, G3, and_5_out, and_6_out, and_7_out, and_8_out);
  and and_7 (and_7_out, P3, P2, P1, G0);
  and and_8 (and_8_out, P3, P2, P1, P0, C0);
  or or_3 (C3, G2, and_9_out, and_11_out, and_10_out);
  and and_9 (and_9_out, P2, G1);
  and and_10 (and_10_out, P2, P1, P0, C0);
  and and_11 (and_11_out, P2, P1, G0);
  or or_4 (C2, G1, and_12_out, and_13_out);
  and and_12 (and_12_out, P1, G0);
  and and_13 (and_13_out, P1, P0, C0);
  or or_5 (C1, G0, and_14_out);
  and and_14 (and_14_out, P0, C0);
endmodule

module \_16位  (
  input  C0,
  input  [15:0] A,
  input  [15:0] B,
  output Gs,
  output Ps,
  output [15:0] S,
  output C16
);

  wire cla_1_gg, cla_1_pg, cla_2_gg, cla_2_pg, cla_3_gg, cla_3_pg, cla_4_gg, cla_4_pg, clu_1_c1, clu_1_c2,
       clu_1_c3;

  // Probe on A
  // Probe on B
  CLA cla_1 (
    .B3(B[3]), .A3(A[3]), .B2(B[2]), .A2(A[2]), .B1(B[1]), .A1(A[1]), .B0(B[0]), .A0(A[0]), .C0(C0),
    .S3(S[3]), .S2(S[2]), .S1(S[1]), .S0(S[0]), .Pg(cla_1_pg), .Gg(cla_1_gg));  // open: C4
  CLA cla_2 (
    .B3(B[7]), .A3(A[7]), .B2(B[6]), .A2(A[6]), .B1(B[5]), .A1(A[5]), .B0(B[4]), .A0(A[4]), .C0(clu_1_c1),
    .S3(S[7]), .S2(S[6]), .S1(S[5]), .S0(S[4]), .Pg(cla_2_pg), .Gg(cla_2_gg));  // open: C4
  CLA cla_3 (
    .B3(B[11]), .A3(A[11]), .B2(B[10]), .A2(A[10]), .B1(B[9]), .A1(A[9]), .B0(B[8]), .A0(A[8]),
    .C0(clu_1_c2), .S3(S[11]), .S2(S[10]), .S1(S[9]), .S0(S[8]), .Pg(cla_3_pg), .Gg(cla_3_gg));  // open: C4
  CLA cla_4 (
    .B3(B[15]), .A3(A[15]), .B2(B[14]), .A2(A[14]), .B1(B[13]), .A1(A[13]), .B0(B[12]), .A0(A[12]),
    .C0(clu_1_c3), .C4(C16), .S3(S[15]), .S2(S[14]), .S1(S[13]), .S0(S[12]), .Pg(cla_4_pg), .Gg(cla_4_gg));
  CLU clu_1 (
    .Gs(Gs), .Ps(Ps), .C3(clu_1_c3), .C2(clu_1_c2), .C1(clu_1_c1), .G3(cla_4_gg), .P3(cla_4_pg),
    .G2(cla_3_gg), .P2(cla_3_pg), .G1(cla_2_gg), .P1(cla_2_pg), .G0(cla_1_gg), .P0(cla_1_pg), .C0(C0));  // open: C4
  // Probe on S
endmodule

module \_32位  (
  input  C0,
  input  [31:0] A,
  input  [31:0] B,
  output [31:0] F,
  output CF,
  output ZF,
  output SF,
  output OF
);

  wire and_1_out, and_2_out, \n16位_1_c16 , \n16位_2_c16 ;

  // Probe on A
  // Probe on B
  \_16位  \u_16位_1  (.C0(C0), .A(A[15:0]), .B(B[15:0]), .S(F[15:0]), .C16(\n16位_1_c16 ));  // open: Gs, Ps
  \_16位  \u_16位_2  (.C0(\n16位_1_c16 ), .A(A[31:16]), .B(B[31:16]), .S(F[31:16]), .C16(\n16位_2_c16 ));  // open: Gs, Ps
  xor xor_1 (CF, \n16位_2_c16 , C0);
  and and_1 (and_1_out, ~A[31], ~B[31], F[15]);  // AND_Gate
  and and_2 (and_2_out, A[31], B[31], ~F[15]);  // AND_Gate
  // Probe on F
  nor nor_1 (ZF, F[16], F[17], F[18], F[19], F[20], F[21], F[22], F[23], F[24], F[25], F[26], F[27], F[28], F[29], F[30], F[31], F[0], F[1], F[2], F[3], F[4], F[5], F[6], F[7], F[8], F[9], F[10], F[11], F[12], F[13], F[14], F[15]);
  or or_1 (OF, and_1_out, and_2_out);

  assign SF = F[15];
endmodule

module ALUstr (
  input  a,
  input  b,
  input  c,
  input  d,
  output SUB,
  output SIG,
  output [1:0] OP
);

  wire and_1_out, not_2_out, not_3_out;

  or or_1 (SUB, c, a);
  not not_1 (SIG, d);
  not not_2 (not_2_out, b);
  and and_1 (and_1_out, not_2_out, c);
  not not_3 (not_3_out, a);
  and and_2 (OP[0], not_3_out, c);
  or or_2 (OP[1], d, and_1_out);
endmodule

module ALU (
  input  [31:0] A,
  input  [31:0] B,
  input  [3:0] ALUstr,
  output ZERO,
  output [31:0] RESULT
);

  wire alustr_1_sig, alustr_1_sub, multiplexer_2_out, \n32位_1_cf , \n32位_1_of , \n32位_1_sf , xor_2_out,
       xor_3_out;
  wire [1:0] alustr_1_op;
  wire [31:0] bit_extender_1_out, bit_extender_2_out, \n32位_1_f , or_1_out, xor_1_out;

  // Probe on A
  // Probe on A
  assign bit_extender_1_out = {{31{alustr_1_sub}}, alustr_1_sub};  // Bit_Extender bit_extender_1
  // Probe on B
  assign xor_1_out = B ^ bit_extender_1_out;  // XOR_Gate xor_1, 32 bits wide
  assign or_1_out = B | A;  // OR_Gate or_1, 32 bits wide
  \_32位  \u_32位_1  (
    .C0(alustr_1_sub), .A(A), .B(xor_1_out), .F(\n32位_1_f ), .CF(\n32位_1_cf ), .ZF(ZERO), .SF(\n32位_1_sf ),
    .OF(\n32位_1_of ));
  // Probe on B
  ALUstr alustr_1 (
    .a(ALUstr[3]), .b(ALUstr[2]), .c(ALUstr[1]), .d(ALUstr[0]), .SUB(alustr_1_sub), .SIG(alustr_1_sig),
    .OP(alustr_1_op));
  xor xor_2 (xor_2_out, alustr_1_sub, \n32位_1_cf );
  xor xor_3 (xor_3_out, \n32位_1_sf , \n32位_1_of );
  Multiplexer #(.select(2), .width(32), .enable("false")) multiplexer_1 (
    .in0(\n32位_1_f ), .in1(or_1_out), .in2(B), .in3(bit_extender_2_out), .out(RESULT), .sel(alustr_1_op));
  Multiplexer #(.enable("false")) multiplexer_2 (
    .in0(xor_2_out), .in1(xor_3_out), .out(multiplexer_2_out), .sel(alustr_1_sig));
  assign bit_extender_2_out = {{31{1'b0}}, multiplexer_2_out};  // Bit_Extender bit_extender_2
  // Probe on RESULT
  // Probe on RESULT
endmodule

module \寄存器  (
  input  [31:0] D,
  input  CLK,
  output [31:0] out_3
);

  Register #(.width(32), .Select("low")) register_1 (.D(D), .Q(out_3), .clk(CLK));  // open: en, clr
endmodule

// 32位寄存器
module \寄存器堆  (
  input  [4:0] RA,
  input  [4:0] RW,
  input  [31:0] Din,
  input  [4:0] RB,
  input  WE,
  input  CLK,
  output [31:0] RDA,
  output [31:0] RDB
);

  wire and_1_out, and_2_out, and_3_out, and_4_out, and_5_out, and_6_out, and_7_out, and_8_out, and_9_out,
       and_10_out, and_11_out, and_12_out, and_13_out, and_14_out, and_15_out, and_16_out, and_17_out,
       and_18_out, and_19_out, and_20_out, and_21_out, and_22_out, and_23_out, and_24_out, and_25_out,
       and_26_out, and_27_out, and_28_out, and_29_out, and_30_out, and_31_out, and_32_out, decoder_1_out0,
       decoder_1_out1, decoder_1_out2, decoder_1_out3, decoder_1_out4, decoder_1_out5, decoder_1_out6,
       decoder_1_out7, decoder_1_out8, decoder_1_out9, decoder_1_out10, decoder_1_out11, decoder_1_out12,
       decoder_1_out13, decoder_1_out14, decoder_1_out15, decoder_1_out16, decoder_1_out17, decoder_1_out18,
       decoder_1_out19, decoder_1_out20, decoder_1_out21, decoder_1_out22, decoder_1_out23, decoder_1_out24,
       decoder_1_out25, decoder_1_out26, decoder_1_out27, decoder_1_out28, decoder_1_out29, decoder_1_out30,
       decoder_1_out31;
  wire [31:0] \寄存器_1_out_3 , \寄存器_2_out_3 , \寄存器_3_out_3 , \寄存器_4_out_3 , \寄存器_5_out_3 , \寄存器_6_out_3 ,
       \寄存器_7_out_3 , \寄存器_8_out_3 , \寄存器_9_out_3 , \寄存器_10_out_3 , \寄存器_11_out_3 , \寄存器_12_out_3 ,
       \寄存器_13_out_3 , \寄存器_14_out_3 , \寄存器_15_out_3 , \寄存器_16_out_3 , \寄存器_17_out_3 , \寄存器_18_out_3 ,
       \寄存器_19_out_3 , \寄存器_20_out_3 , \寄存器_22_out_3 , \寄存器_23_out_3 , \寄存器_24_out_3 , \寄存器_25_out_3 ,
       \寄存器_26_out_3 , \寄存器_27_out_3 , \寄存器_28_out_3 , \寄存器_29_out_3 , \寄存器_30_out_3 , \寄存器_31_out_3 ,
       \寄存器_32_out_3 ;

  Decoder #(.select(5), .enable("false")) decoder_1 (
    .out0(decoder_1_out0), .out1(decoder_1_out1), .out2(decoder_1_out2), .out3(decoder_1_out3),
    .out4(decoder_1_out4), .out5(decoder_1_out5), .out6(decoder_1_out6), .out7(decoder_1_out7),
    .out8(decoder_1_out8), .out9(decoder_1_out9), .out10(decoder_1_out10), .out11(decoder_1_out11),
    .out12(decoder_1_out12), .out13(decoder_1_out13), .out14(decoder_1_out14), .out15(decoder_1_out15),
    .out16(decoder_1_out16), .out17(decoder_1_out17), .out18(decoder_1_out18), .out19(decoder_1_out19),
    .out20(decoder_1_out20), .out21(decoder_1_out21), .out22(decoder_1_out22), .out23(decoder_1_out23),
    .out24(decoder_1_out24), .out25(decoder_1_out25), .out26(decoder_1_out26), .out27(decoder_1_out27),
    .out28(decoder_1_out28), .out29(decoder_1_out29), .out30(decoder_1_out30), .out31(decoder_1_out31),
    .sel(RW));
  and and_1 (and_1_out, WE, CLK, decoder_1_out0);
  and and_2 (and_2_out, WE, CLK, decoder_1_out1);
  and and_3 (and_3_out, WE, CLK, decoder_1_out2);
  and and_4 (and_4_out, WE, CLK, decoder_1_out3);
  and and_5 (and_5_out, WE, CLK, decoder_1_out4);
  and and_6 (and_6_out, WE, CLK, decoder_1_out5);
  and and_7 (and_7_out, WE, CLK, decoder_1_out6);
  and and_8 (and_8_out, WE, CLK, decoder_1_out7);
  and and_9 (and_9_out, WE, CLK, decoder_1_out8);
  and and_10 (and_10_out, WE, CLK, decoder_1_out9);
  and and_11 (and_11_out, WE, CLK, decoder_1_out10);
  and and_12 (and_12_out, WE, CLK, decoder_1_out11);
  and and_13 (and_13_out, WE, CLK, decoder_1_out12);
  and and_14 (and_14_out, WE, CLK, decoder_1_out13);
  and and_15 (and_15_out, WE, CLK, decoder_1_out14);
  and and_16 (and_16_out, WE, CLK, decoder_1_out15);
  and and_17 (and_17_out, WE, CLK, decoder_1_out16);
  and and_18 (and_18_out, WE, CLK, decoder_1_out17);
  and and_19 (and_19_out, WE, CLK, decoder_1_out18);
  and and_20 (and_20_out, WE, CLK, decoder_1_out19);
  and and_21 (and_21_out, WE, CLK, decoder_1_out20);
  and and_22 (and_22_out, WE, CLK, decoder_1_out21);
  and and_23 (and_23_out, WE, CLK, decoder_1_out22);
  and and_24 (and_24_out, WE, CLK, decoder_1_out23);
  and and_25 (and_25_out, WE, CLK, decoder_1_out24);
  and and_26 (and_26_out, WE, CLK, decoder_1_out25);
  and and_27 (and_27_out, WE, CLK, decoder_1_out26);
  and and_28 (and_28_out, WE, CLK, decoder_1_out27);
  and and_29 (and_29_out, WE, CLK, decoder_1_out28);
  and and_30 (and_30_out, WE, CLK, decoder_1_out29);
  and and_31 (and_31_out, WE, CLK, decoder_1_out30);
  and and_32 (and_32_out, WE, CLK, decoder_1_out31);
  \寄存器  \u_寄存器_1  (.D(Din), .out_3(\寄存器_1_out_3 ), .CLK(and_1_out));
  \寄存器  \u_寄存器_2  (.D(Din), .out_3(\寄存器_2_out_3 ), .CLK(and_2_out));
  \寄存器  \u_寄存器_3  (.D(Din), .out_3(\寄存器_3_out_3 ), .CLK(and_3_out));
  \寄存器  \u_寄存器_4  (.D(Din), .out_3(\寄存器_4_out_3 ), .CLK(and_4_out));
  \寄存器  \u_寄存器_5  (.D(Din), .out_3(\寄存器_5_out_3 ), .CLK(and_5_out));
  \寄存器  \u_寄存器_6  (.D(Din), .out_3(\寄存器_6_out_3 ), .CLK(and_6_out));
  \寄存器  \u_寄存器_7  (.D(Din), .out_3(\寄存器_7_out_3 ), .CLK(and_7_out));
  \寄存器  \u_寄存器_8  (.D(Din), .out_3(\寄存器_8_out_3 ), .CLK(and_8_out));
  \寄存器  \u_寄存器_9  (.D(Din), .out_3(\寄存器_9_out_3 ), .CLK(and_9_out));
  \寄存器  \u_寄存器_10  (.D(Din), .out_3(\寄存器_10_out_3 ), .CLK(and_10_out));
  \寄存器  \u_寄存器_11  (.D(Din), .out_3(\寄存器_11_out_3 ), .CLK(and_11_out));
  \寄存器  \u_寄存器_12  (.D(Din), .out_3(\寄存器_12_out_3 ), .CLK(and_12_out));
  \寄存器  \u_寄存器_13  (.D(Din), .out_3(\寄存器_13_out_3 ), .CLK(and_13_out));
  \寄存器  \u_寄存器_14  (.D(Din), .out_3(\寄存器_14_out_3 ), .CLK(and_14_out));
  \寄存器  \u_寄存器_15  (.D(Din), .out_3(\寄存器_15_out_3 ), .CLK(and_15_out));
  \寄存器  \u_寄存器_16  (.D(Din), .out_3(\寄存器_16_out_3 ), .CLK(and_16_out));
  \寄存器  \u_寄存器_17  (.D(Din), .out_3(\寄存器_17_out_3 ), .CLK(and_17_out));
  \寄存器  \u_寄存器_18  (.D(Din), .out_3(\寄存器_18_out_3 ), .CLK(and_18_out));
  \寄存器  \u_寄存器_19  (.D(Din), .out_3(\寄存器_19_out_3 ), .CLK(and_19_out));
  \寄存器  \u_寄存器_20  (.D(Din), .out_3(\寄存器_20_out_3 ), .CLK(and_20_out));
  \寄存器  \u_寄存器_21  (.D(Din), .out_3(\寄存器_20_out_3 ), .CLK(and_21_out));
  \寄存器  \u_寄存器_22  (.D(Din), .out_3(\寄存器_22_out_3 ), .CLK(and_22_out));
  \寄存器  \u_寄存器_23  (.D(Din), .out_3(\寄存器_23_out_3 ), .CLK(and_23_out));
  \寄存器  \u_寄存器_24  (.D(Din), .out_3(\寄存器_24_out_3 ), .CLK(and_24_out));
  \寄存器  \u_寄存器_25  (.D(Din), .out_3(\寄存器_25_out_3 ), .CLK(and_25_out));
  \寄存器  \u_寄存器_26  (.D(Din), .out_3(\寄存器_26_out_3 ), .CLK(and_26_out));
  \寄存器  \u_寄存器_27  (.D(Din), .out_3(\寄存器_27_out_3 ), .CLK(and_27_out));
  \寄存器  \u_寄存器_28  (.D(Din), .out_3(\寄存器_28_out_3 ), .CLK(and_28_out));
  \寄存器  \u_寄存器_29  (.D(Din), .out_3(\寄存器_29_out_3 ), .CLK(and_29_out));
  \寄存器  \u_寄存器_30  (.D(Din), .out_3(\寄存器_30_out_3 ), .CLK(and_30_out));
  \寄存器  \u_寄存器_31  (.D(Din), .out_3(\寄存器_31_out_3 ), .CLK(and_31_out));
  \寄存器  \u_寄存器_32  (.D(Din), .out_3(\寄存器_32_out_3 ), .CLK(and_32_out));
  Multiplexer #(.select(5), .width(32), .enable("false")) multiplexer_1 (
    .in0(\寄存器_1_out_3 ), .in1(\寄存器_2_out_3 ), .in2(\寄存器_3_out_3 ), .in3(\寄存器_4_out_3 ), .in4(\寄存器_5_out_3 ),
    .in5(\寄存器_6_out_3 ), .in6(\寄存器_7_out_3 ), .in7(\寄存器_8_out_3 ), .in8(\寄存器_9_out_3 ), .in9(\寄存器_10_out_3 ),
    .in10(\寄存器_11_out_3 ), .in11(\寄存器_12_out_3 ), .in12(\寄存器_13_out_3 ), .in13(\寄存器_14_out_3 ),
    .in14(\寄存器_15_out_3 ), .in15(\寄存器_16_out_3 ), .in16(\寄存器_17_out_3 ), .in17(\寄存器_18_out_3 ),
    .in18(\寄存器_19_out_3 ), .in19(\寄存器_20_out_3 ), .in20(\寄存器_20_out_3 ), .in21(\寄存器_22_out_3 ),
    .in22(\寄存器_23_out_3 ), .in23(\寄存器_24_out_3 ), .in24(\寄存器_25_out_3 ), .in25(\寄存器_26_out_3 ),
    .in26(\寄存器_27_out_3 ), .in27(\寄存器_28_out_3 ), .in28(\寄存器_29_out_3 ), .in29(\寄存器_30_out_3 ),
    .in30(\寄存器_31_out_3 ), .in31(\寄存器_32_out_3 ), .out(RDA), .sel(RA));
  Multiplexer #(.select(5), .width(32), .enable("false")) multiplexer_2 (
    .in0(\寄存器_1_out_3 ), .in1(\寄存器_2_out_3 ), .in2(\寄存器_3_out_3 ), .in3(\寄存器_4_out_3 ), .in4(\寄存器_5_out_3 ),
    .in5(\寄存器_6_out_3 ), .in6(\寄存器_7_out_3 ), .in7(\寄存器_8_out_3 ), .in8(\寄存器_9_out_3 ), .in9(\寄存器_10_out_3 ),
    .in10(\寄存器_11_out_3 ), .in11(\寄存器_12_out_3 ), .in12(\寄存器_13_out_3 ), .in13(\寄存器_14_out_3 ),
    .in14(\寄存器_15_out_3 ), .in15(\寄存器_16_out_3 ), .in16(\寄存器_17_out_3 ), .in17(\寄存器_18_out_3 ),
    .in18(\寄存器_19_out_3 ), .in19(\寄存器_20_out_3 ), .in20(\寄存器_20_out_3 ), .in21(\寄存器_22_out_3 ),
    .in22(\寄存器_23_out_3 ), .in23(\寄存器_24_out_3 ), .in24(\寄存器_25_out_3 ), .in25(\寄存器_26_out_3 ),
    .in26(\寄存器_27_out_3 ), .in27(\寄存器_28_out_3 ), .in28(\寄存器_29_out_3 ), .in29(\寄存器_30_out_3 ),
    .in30(\寄存器_31_out_3 ), .in31(\寄存器_32_out_3 ), .out(RDB), .sel(RB));
endmodule

module \取指令通路  (
  input  [31:0] imm,
  input  [2:0] extop,
  input  in_3,
  input  in_4,
  input  in_5,
  output [31:0] instr,
  output [6:0] op,
  output [4:0] rd,
  output [2:0] funct3,
  output [4:0] Rs1,
  output [4:0] Rs2,
  output [6:0] funct7,
  output [31:0] imm_2
);

  wire and_1_out, Clock, or_1_out, \复位按钮_2_out , \复位按钮_out ;
  wire [31:0] adder_1_out, multiplexer_1_out, PC_q;

  Register #(.width(32), .Select("low")) PC (.D(adder_1_out), .en(1'b1), .Q(PC_q), .clk(Clock), .clr(\复位按钮_out ));
  Button \u_复位按钮  (.out(\复位按钮_out ));
  Clock clock_1 (.out(Clock));
  or or_1 (or_1_out, in_3, and_1_out);
  Multiplexer #(.width(32), .enable("false")) multiplexer_1 (
    .in0(32'h4), .in1(imm), .out(multiplexer_1_out), .sel(or_1_out));
  and and_1 (and_1_out, in_4, in_5);
  Button \u_复位按钮_2  (.out(\复位按钮_2_out ));
  Adder #(.width(32)) adder_1 (.a(PC_q), .b(multiplexer_1_out), .out(adder_1_out));  // open: cin, cout
  RAM #(.addrWidth(10), .dataWidth(32), .bus("asynch"), .Select("low")) \u_指令寄存器RAM  (
    .addr(PC_q[9:0]), .data({funct7, instr[24:15], funct3, instr[11:0]}), .clr(\复位按钮_2_out ));  // open: sel, ld
  \立即数拓展器  \u_立即数拓展器_1  (.instr({funct7, instr[24:15], funct3, instr[11:0]}), .extop(extop), .imm(imm_2));

  assign {instr[31:25], instr[14:12]} = {funct7, funct3};
  assign op = instr[6:0];
  assign rd = instr[11:7];
  assign Rs1 = instr[19:15];
  assign Rs2 = instr[24:20];

  // Other names for the same wires on the sheet: Branch = in_4; Jump = in_3; Zero = in_5
endmodule

module \立即数拓展器  (
  input  [31:0] instr,
  input  [2:0] extop,
  output [31:0] imm
);

  wire [11:0] bit_extender_4_out;
  wire [19:0] bit_extender_1_out, bit_extender_2_out, bit_extender_3_out;

  assign bit_extender_1_out = {{19{instr[31]}}, instr[31]};  // Bit_Extender bit_extender_1
  assign bit_extender_2_out = {{19{instr[31]}}, instr[31]};  // Bit_Extender bit_extender_2
  assign bit_extender_3_out = {{19{instr[31]}}, instr[31]};  // Bit_Extender bit_extender_3
  assign bit_extender_4_out = {{11{instr[31]}}, instr[31]};  // Bit_Extender bit_extender_4
  Multiplexer #(.select(3), .width(32), .enable("false")) multiplexer_1 (
    .in0({bit_extender_1_out, instr[31:20]}), .in1({instr[31:12], {12{1'b0}}}),
    .in2({bit_extender_2_out, instr[31:25], instr[11:7]}),
    .in3({bit_extender_3_out, instr[7], instr[30:25], instr[11:8], 1'b1}),
    .in4({bit_extender_4_out, instr[19:12], instr[20], instr[30:21], 1'b1}), .in5({32{1'b0}}),
    .in6({32{1'b0}}), .in7({32{1'b0}}), .out(imm), .sel(extop));
endmodule

module CPU (
  output [31:0] Instr,
  output out_2,
  output out_3,
  output out_4,
  output [1:0] out_5,
  output [3:0] out_6,
  output out_7,
  output [6:0] op,
  output out_9,
  output [4:0] Rd,
  output [2:0] funct3,
  output out_12,
  output [4:0] Rs1,
  output [2:0] out_14,
  output [4:0] Rs2,
  output [6:0] funct7,
  output [31:0] imm
);

  wire alu_1_zero, and_1_out, and_2_out, and_3_out, and_4_out, clk, lui_out, or_1_out, or_2_out, ori_out,
       RESET, sltu_out;
  wire [31:0] adder_1_out, alu_1_result, multiplexer_1_out, multiplexer_2_out, multiplexer_3_out,
       multiplexer_4_out, PC_q, ram_1_data, \寄存器堆_1_rda , \寄存器堆_1_rdb ;

  \立即数拓展器  \u_立即数拓展器_1  (.instr({funct7, Instr[24:15], funct3, Instr[11:0]}), .extop({out_3, out_14[1:0]}), .imm(imm));
  Clock u_clk (.out(clk));
  Button u_RESET (.out(RESET));
  \寄存器堆  \u_寄存器堆_1  (
    .RA(Instr[19:15]), .Din(multiplexer_4_out), .RB(Instr[24:20]), .WE(out_9), .CLK(clk), .RDA(\寄存器堆_1_rda ),
    .RDB(\寄存器堆_1_rdb ), .RW(Instr[11:7]));
  // AND_Gate add has open pins: in0=Instr[6], in1=Instr[5], in2=Instr[4], in3=Instr[3], in4=Instr[2], in5=Instr[1], in6=Instr[0], out=open
  Register #(.width(32), .trigger("falling"), .Select("low")) PC (
    .D(adder_1_out), .Q(PC_q), .clk(clk), .clr(RESET));  // open: en
  // AND_Gate slt has open pins: in0=Instr[6], in1=Instr[5], in2=Instr[4], in3=Instr[3], in4=Instr[2], in5=Instr[1], in6=Instr[0], out=open
  Multiplexer #(.width(32), .enable("false")) multiplexer_1 (
    .in0(\寄存器堆_1_rda ), .in1(PC_q), .out(multiplexer_1_out), .sel(out_3));
  Multiplexer #(.select(2), .width(32), .enable("false")) multiplexer_2 (
    .in0(\寄存器堆_1_rdb ), .in1(32'h4), .in2(imm), .out(multiplexer_2_out), .sel({out_5[1], out_3}));  // open: in3
  and sltu (sltu_out, ~Instr[6], Instr[5], Instr[4], ~Instr[3], ~Instr[2], Instr[1], Instr[0]);  // AND_Gate
  Multiplexer #(.width(32), .enable("false")) multiplexer_3 (
    .in0(32'h4), .in1(imm), .out(multiplexer_3_out), .sel(or_1_out));
  or or_1 (or_1_out, out_3, and_1_out);
  and and_1 (and_1_out, out_2, alu_1_zero);
  ALU alu_1 (.ZERO(alu_1_zero), .RESULT(alu_1_result), .ALUstr(out_6), .A(multiplexer_1_out), .B(multiplexer_2_out));
  or or_2 (or_2_out, sltu_out, ori_out);
  Adder #(.width(32)) adder_1 (.a(PC_q), .b(multiplexer_3_out), .out(adder_1_out));  // open: cin, cout
  and ori (ori_out, ~Instr[6], ~Instr[5], Instr[4], ~Instr[3], ~Instr[2], Instr[1], Instr[0]);  // AND_Gate
  RAM #(.addrWidth(12), .dataWidth(32), .bus("separate"), .Select("low")) ram_1 (
    .addr(alu_1_result[13:2]), .din(\寄存器堆_1_rdb ), .data(ram_1_data), .str(out_12), .clk(clk), .ld(1'b1),
    .clr(RESET));  // open: sel
  and lui (lui_out, ~Instr[6], Instr[5], Instr[4], ~Instr[3], Instr[2], Instr[1], Instr[0]);  // AND_Gate
  and and_2 (and_2_out, or_2_out, funct3[2]);
  and and_3 (and_3_out, or_2_out, funct3[1]);
  and and_4 (and_4_out, or_2_out, funct3[0]);
  Multiplexer #(.width(32), .enable("false")) multiplexer_4 (
    .in0(alu_1_result), .in1(ram_1_data), .out(multiplexer_4_out), .sel(out_7));
  and Iw (out_7, ~Instr[6], ~Instr[5], ~Instr[4], ~Instr[3], ~Instr[2], Instr[1], Instr[0]);  // AND_Gate
  RAM #(.addrWidth(12), .dataWidth(32), .Select("low")) ram_2 (
    .addr(PC_q[13:2]), .data({funct7, Instr[24:15], funct3, Instr[11:0]}), .clr(RESET));  // open: sel, clk, ld
  and sw (out_12, ~Instr[6], Instr[5], ~Instr[4], ~Instr[3], ~Instr[2], Instr[1], Instr[0]);  // AND_Gate
  and beq (out_2, Instr[6], Instr[5], ~Instr[4], ~Instr[3], ~Instr[2], Instr[1], Instr[0]);  // AND_Gate
  and jal (out_3, Instr[6], Instr[5], ~Instr[4], Instr[3], Instr[2], Instr[1], Instr[0]);  // AND_Gate
  or or_3 (out_9, sltu_out, ori_out, lui_out, out_7, out_3);
  or or_4 (out_6[3], lui_out, out_2);
  or or_5 (out_6[2], lui_out, and_2_out);
  or or_6 (out_6[1], lui_out, and_3_out);
  or or_7 (out_6[0], lui_out, and_4_out);
  or or_8 (out_5[1], ori_out, lui_out, out_7, out_12);
  or or_9 (out_14[1], out_2, out_12);
  or or_10 (out_14[0], lui_out, out_2);

  assign {Instr[31:25], Instr[14:12]} = {funct7, funct3};
  assign op = Instr[6:0];
  assign out_4 = out_3;
  assign out_5[0] = out_3;
  assign out_14[2] = out_3;
  assign Rd = Instr[11:7];
  assign Rs1 = Instr[19:15];
  assign Rs2 = Instr[24:20];

  // Other names for the same wires on the sheet: ALUBSrc[1:0] = {out_5[1], out_3}; ALUctr[3:0] = out_6;
  //   Branch = out_2; ExtOp[2:0] = {out_3, out_14[1:0]}; ALUASrc = out_3; Jump = out_3; MemtoReg = out_7;
  //   MemWr = out_12; RegWr = out_9
endmodule
