// Logisim project lab4.circ as structural Verilog: 6 circuits, main circuit CLA
module CLA (
  input  B3,
  input  A3,
  input  B2,
  input  A2,
  input  B1,
  input  A1,
  input  B0,
  input  A0,
  input  C0,
  output C4,
  output S3,
  output S2,
  output S1,
  output S0,
  output Pg,
  output Gg
);

  wire and_1_out, and_2_out, and_3_out, and_4_out, and_5_out, and_6_out, and_7_out, and_9_out, and_10_out,
       and_11_out, nand_1_out, nand_2_out, nand_3_out, nand_4_out, nor_1_out, nor_2_out, nor_3_out,
       nor_4_out, not_1_out, not_2_out, not_3_out, not_4_out, not_5_out, not_6_out, or_1_out, or_2_out,
       or_3_out, or_4_out, or_5_out, or_6_out, or_7_out, or_8_out, or_9_out, or_10_out;

  nand nand_1 (nand_1_out, B3, A3);
  nor nor_1 (nor_1_out, B3, A3);
  nand nand_2 (nand_2_out, B2, A2);
  nor nor_2 (nor_2_out, B2, A2);
  nand nand_3 (nand_3_out, B1, A1);
  nor nor_3 (nor_3_out, B1, A1);
  nand nand_4 (nand_4_out, B0, A0);
  nor nor_4 (nor_4_out, B0, A0);
  not not_1 (not_1_out, C0);
  not not_2 (not_2_out, nor_1_out);
  or or_1 (or_1_out, ~nor_2_out, ~nand_1_out);  // OR_Gate
  or or_2 (or_2_out, ~nor_3_out, ~nand_1_out, ~nand_2_out);  // OR_Gate
  or or_3 (or_3_out, ~nor_4_out, ~nand_1_out, ~nand_2_out, ~nand_3_out);  // OR_Gate
  or or_4 (or_4_out, ~nand_1_out, ~nand_2_out, ~nand_3_out, ~nand_4_out, ~not_1_out);  // OR_Gate
  and and_1 (and_1_out, nand_1_out, ~nor_1_out);  // AND_Gate
  not not_3 (not_3_out, nor_2_out);
  or or_5 (or_5_out, ~nor_3_out, ~nand_2_out);  // OR_Gate
  or or_6 (or_6_out, ~nor_4_out, ~nand_2_out, ~nand_3_out);  // OR_Gate
  or or_7 (or_7_out, ~nand_2_out, ~nand_3_out, ~nand_4_out, ~not_1_out);  // OR_Gate
  and and_2 (and_2_out, nand_2_out, ~nor_2_out);  // AND_Gate
  not not_4 (not_4_out, nor_3_out);
  or or_8 (or_8_out, ~nor_4_out, ~nand_3_out);  // OR_Gate
  or or_9 (or_9_out, ~nand_3_out, ~nand_4_out, ~not_1_out);  // OR_Gate
  and and_3 (and_3_out, nand_3_out, ~nor_3_out);  // AND_Gate
  not not_5 (not_5_out, nor_4_out);
  or or_10 (or_10_out, ~nand_4_out, ~not_1_out);  // OR_Gate
  and and_4 (and_4_out, nand_4_out, ~nor_4_out);  // AND_Gate
  not not_6 (not_6_out, not_1_out);
  and and_5 (and_5_out, ~nor_1_out, ~nand_2_out);  // AND_Gate
  and and_6 (and_6_out, ~nor_1_out, ~nor_2_out, ~nand_3_out);  // AND_Gate
  and and_7 (and_7_out, ~nor_1_out, ~nor_2_out, ~nor_3_out, nand_4_out);  // AND_Gate
  and and_8 (C4, not_2_out, or_1_out, or_2_out, or_3_out, or_4_out);
  and and_9 (and_9_out, not_3_out, or_5_out, or_6_out, or_7_out);
  and and_10 (and_10_out, not_4_out, or_8_out, or_9_out);
  and and_11 (and_11_out, not_5_out, or_10_out);
  and and_12 (Pg, ~nor_1_out, ~nor_2_out, ~nor_3_out, ~nor_4_out);  // AND_Gate
  xor xor_1 (S3, and_1_out, and_9_out);
  xor xor_2 (S2, and_2_out, and_10_out);
  xor xor_3 (S1, and_3_out, and_11_out);
  xor xor_4 (S0, and_4_out, not_6_out);
  or or_11 (Gg, ~nand_1_out, and_5_out, and_6_out, and_7_out);  // OR_Gate
endmodule

module CLU (
  input  C0,
  input  G3,
  input  P3,
  input  G2,
  input  P2,
  input  G1,
  input  P1,
  input  G0,
  input  P0,
  output Gs,
  output C3,
  output C2,
  output C1,
  output Ps,
  output C4
);

  wire and_1_out, and_2_out, and_3_out, and_5_out, and_6_out, and_7_out, and_8_out, and_9_out, and_10_out,
       and_11_out, and_12_out, and_13_out, and_14_out;

  and and_1 (and_1_out, P3, P2, P1, G0);
  or or_1 (Gs, and_1_out, and_3_out, and_2_out, G3);
  and and_2 (and_2_out, G2, P3);
  and and_3 (and_3_out, G1, P2, P3);
  and and_4 (Ps, P3, P2, P1, P0);
  and and_5 (and_5_out, P3, G2);
  and and_6 (and_6_out, P3, P2, G1);
  or or_2 (C4, G3, and_5_out, and_6_out, and_7_out, and_8_out);
  and and_7 (and_7_out, P3, P2, P1, G0);
  and and_8 (and_8_out, P3, P2, P1, P0, C0);
  or or_3 (C3, G2, and_9_out, and_10_out, and_11_out);
  and and_9 (and_9_out, P2, G1);
  and and_10 (and_10_out, P2, P1, G0);
  and and_11 (and_11_out, P2, P1, P0, C0);
  or or_4 (C2, G1, and_12_out, and_13_out);
  and and_12 (and_12_out, P1, G0);
  and and_13 (and_13_out, P1, P0, C0);
  or or_5 (C1, G0, and_14_out);
  and and_14 (and_14_out, P0, C0);
endmodule

module \_16位先行进位加法器  (
  input  C0,
  input  [15:0] A,
  input  [15:0] B,
  output Gs,
  output Ps,
  output [15:0] S,
  output C16
);

  wire cla_1_gg, cla_1_pg, cla_2_gg, cla_2_pg, cla_3_gg, cla_3_pg, cla_4_gg, cla_4_pg, clu_1_c1, clu_1_c2,
       clu_1_c3;

  // Probe on A
  // Probe on B
  CLA cla_1 (
    .B3(B[3]), .A3(A[3]), .B2(B[2]), .A2(A[2]), .B1(B[1]), .A1(A[1]), .B0(B[0]), .A0(A[0]), .C0(C0),
    .S3(S[3]), .S2(S[2]), .S1(S[1]), .S0(S[0]), .Pg(cla_1_pg), .Gg(cla_1_gg));  // open: C4
  CLA cla_2 (
    .B3(B[7]), .A3(A[7]), .B2(B[6]), .A2(A[6]), .B1(B[5]), .A1(A[5]), .B0(B[4]), .A0(A[4]), .C0(clu_1_c1),
    .S3(S[7]), .S2(S[6]), .S1(S[5]), .S0(S[4]), .Pg(cla_2_pg), .Gg(cla_2_gg));  // open: C4
  CLA cla_3 (
    .B3(B[11]), .A3(A[11]), .B2(B[10]), .A2(A[10]), .B1(B[9]), .A1(A[9]), .B0(B[8]), .A0(A[8]),
    .C0(clu_1_c2), .S3(S[11]), .S2(S[10]), .S1(S[9]), .S0(S[8]), .Pg(cla_3_pg), .Gg(cla_3_gg));  // open: C4
  CLA cla_4 (
    .B3(B[15]), .A3(A[15]), .B2(B[14]), .A2(A[14]), .B1(B[13]), .A1(A[13]), .B0(B[12]), .A0(A[12]),
    .C0(clu_1_c3), .C4(C16), .S3(S[15]), .S2(S[14]), .S1(S[13]), .S0(S[12]), .Pg(cla_4_pg), .Gg(cla_4_gg));
  CLU clu_1 (
    .C3(clu_1_c3), .C2(clu_1_c2), .C1(clu_1_c1), .G3(cla_4_gg), .P3(cla_4_pg), .G2(cla_3_gg), .P2(cla_3_pg),
    .G1(cla_2_gg), .P1(cla_2_pg), .G0(cla_1_gg), .P0(cla_1_pg), .C0(C0), .Ps(Ps), .Gs(Gs));  // open: C4
  // Probe on S
endmodule

// 32位
module \_32位先行进位加法器  (
  input  C0,
  input  [31:0] A,
  input  [31:0] B,
  output [31:0] F,
  output CF,
  output ZF,
  output SF,
  output OF
);

  wire and_1_out, and_2_out, \n16位先行进位加法器_1_c16 , \n16位先行进位加法器_2_c16 ;

  // Probe on A
  // Probe on B
  \_16位先行进位加法器  \u_16位先行进位加法器_1  (
    .C0(C0), .A(A[15:0]), .B(B[15:0]), .S(F[15:0]), .C16(\n16位先行进位加法器_1_c16 ));  // open: Gs, Ps
  \_16位先行进位加法器  \u_16位先行进位加法器_2  (
    .C0(\n16位先行进位加法器_1_c16 ), .A(A[31:16]), .B(B[31:16]), .S(F[31:16]), .C16(\n16位先行进位加法器_2_c16 ));  // open: Gs, Ps
  and and_1 (and_1_out, ~A[31], ~B[31], F[15]);  // AND_Gate
  and and_2 (and_2_out, A[31], B[31], ~F[15]);  // AND_Gate
  xor xor_1 (CF, \n16位先行进位加法器_2_c16 , C0);
  // Probe on F
  nor nor_1 (ZF, F[16], F[17], F[18], F[19], F[20], F[21], F[22], F[23], F[24], F[25], F[26], F[27], F[28], F[29], F[30], F[31], F[0], F[1], F[2], F[3], F[4], F[5], F[6], F[7], F[8], F[9], F[10], F[11], F[12], F[13], F[14], F[15]);
  or or_1 (OF, and_1_out, and_2_out);

  assign SF = F[15];
endmodule

module ALU (
  input  [31:0] A,
  input  [31:0] B,
  input  [3:0] ALUstr,
  output ZERO,
  output [31:0] RESULT
);

  wire aluctr_1_sig, aluctr_1_sub, multiplexer_2_out, \n32位先行进位加法器_1_cf , \n32位先行进位加法器_1_of ,
       \n32位先行进位加法器_1_sf , xor_2_out, xor_3_out;
  wire [1:0] aluctr_1_op;
  wire [31:0] bit_extender_1_out, bit_extender_2_out, \n32位先行进位加法器_1_f , or_1_out, xor_1_out;

  // Probe on A
  // Probe on A
  assign bit_extender_1_out = {{31{aluctr_1_sub}}, aluctr_1_sub};  // Bit_Extender bit_extender_1
  // Probe on B
  assign xor_1_out = B ^ bit_extender_1_out;  // XOR_Gate xor_1, 32 bits wide
  \_32位先行进位加法器  \u_32位先行进位加法器_1  (
    .C0(aluctr_1_sub), .A(A), .B(xor_1_out), .F(\n32位先行进位加法器_1_f ), .CF(\n32位先行进位加法器_1_cf ), .ZF(ZERO),
    .SF(\n32位先行进位加法器_1_sf ), .OF(\n32位先行进位加法器_1_of ));
  assign or_1_out = B | A;  // OR_Gate or_1, 32 bits wide
  // Probe on B
  ALUctr aluctr_1 (
    .a(ALUstr[3]), .b(ALUstr[2]), .c(ALUstr[1]), .d(ALUstr[0]), .SUB(aluctr_1_sub), .SIG(aluctr_1_sig),
    .OP(aluctr_1_op));
  xor xor_2 (xor_2_out, aluctr_1_sub, \n32位先行进位加法器_1_cf );
  xor xor_3 (xor_3_out, \n32位先行进位加法器_1_sf , \n32位先行进位加法器_1_of );
  Multiplexer #(.select(2), .width(32), .enable("false")) multiplexer_1 (
    .in0(\n32位先行进位加法器_1_f ), .in1(or_1_out), .in2(B), .in3(bit_extender_2_out), .out(RESULT),
    .sel(aluctr_1_op));
  Multiplexer #(.enable("false")) multiplexer_2 (
    .in0(xor_2_out), .in1(xor_3_out), .out(multiplexer_2_out), .sel(aluctr_1_sig));
  assign bit_extender_2_out = {{31{1'b0}}, multiplexer_2_out};  // Bit_Extender bit_extender_2
  // Probe on RESULT
  // Probe on RESULT
endmodule

module ALUctr (
  input  a,
  input  b,
  input  c,
  input  d,
  output SUB,
  output SIG,
  output [1:0] OP
);

  wire and_1_out, not_2_out, not_3_out;

  or or_1 (SUB, c, a);
  not not_1 (SIG, d);
  not not_2 (not_2_out, b);
  not not_3 (not_3_out, a);
  and and_1 (and_1_out, not_2_out, c);
  and and_2 (OP[0], not_3_out, c);
  or or_2 (OP[1], d, and_1_out);
endmodule
